// Logisim project 8bitCpu.circ as structural Verilog
module ALU (
  input  [7:0] A,
  input  [7:0] B,
  input  [1:0] Operation,
  output [7:0] Result,
  output Zero
);

  wire [7:0] adder_1_out, and_1_out, or_1_out, subtractor_1_out;

  Adder adder_1 (.a(A), .b(B), .out(adder_1_out), .cin(1'b0));  // open: cout
  Subtractor subtractor_1 (.a(A), .b(B), .out(subtractor_1_out), .bin(1'b0));  // open: bout
  assign and_1_out = A & B;  // AND_Gate and_1, 8 bits wide
  assign or_1_out = A | B;  // OR_Gate or_1, 8 bits wide
  Multiplexer #(.select(2), .width(8)) multiplexer_1 (
    .in0(adder_1_out), .in1(subtractor_1_out), .in2(and_1_out), .in3(or_1_out), .out(Result), .sel(Operation));
  Comparator comparator_1 (.a(Result), .b({8{1'b0}}), .eq(Zero));  // open: gt, lt
endmodule

module Registers (
  input  clock,
  input  write_enable,
  input  [1:0] write_addr,
  input  [7:0] write_data,
  input  [1:0] read_addr_a,
  input  [1:0] read_addr_b,
  output [7:0] read_data_a,
  output [7:0] read_data_b
);

  wire and_1_out, and_2_out, and_3_out, and_4_out, decoder_1_out0, decoder_1_out1, decoder_1_out2,
       decoder_1_out3;
  wire [7:0] R0_q, R1_q, R2_q, R3_q;

  Decoder #(.enable("false"), .select(2)) decoder_1 (
    .out0(decoder_1_out0), .out1(decoder_1_out1), .out2(decoder_1_out2), .out3(decoder_1_out3),
    .sel(write_addr));
  and and_1 (and_1_out, decoder_1_out0, write_enable);
  and and_2 (and_2_out, decoder_1_out1, write_enable);
  and and_3 (and_3_out, decoder_1_out2, write_enable);
  and and_4 (and_4_out, decoder_1_out3, write_enable);
  Register R0 (.D(write_data), .en(and_1_out), .clk(clock), .Q(R0_q));  // open: clr
  Register R1 (.D(write_data), .en(and_2_out), .clk(clock), .Q(R1_q));  // open: clr
  Register R2 (.D(write_data), .en(and_3_out), .clk(clock), .Q(R2_q));  // open: clr
  Register R3 (.D(write_data), .en(and_4_out), .clk(clock), .Q(R3_q));  // open: clr
  Multiplexer #(.select(2), .width(8)) multiplexer_1 (
    .in0(R0_q), .in1(R1_q), .in2(R2_q), .in3(R3_q), .out(read_data_a), .sel(read_addr_a));
  Multiplexer #(.select(2), .width(8)) multiplexer_2 (
    .in0(R0_q), .in1(R1_q), .in2(R2_q), .in3(R3_q), .out(read_data_b), .sel(read_addr_b));
endmodule

module PC (
  input  clock,
  input  pc_increment,
  input  pc_load,
  input  [7:0] pc_load_value,
  input  pc_reset,
  output [7:0] pc_value
);

  wire [7:0] adder_1_out, multiplexer_1_out, multiplexer_2_out;

  Adder adder_1 (.a(pc_value), .b(8'h1), .out(adder_1_out));  // open: cin, cout
  Multiplexer #(.width(8)) multiplexer_1 (
    .in0(pc_value), .in1(adder_1_out), .out(multiplexer_1_out), .sel(pc_increment));
  Multiplexer #(.width(8)) multiplexer_2 (
    .in0(multiplexer_1_out), .in1(pc_load_value), .out(multiplexer_2_out), .sel(pc_load));
  Register register_1 (.D(multiplexer_2_out), .en(1'b1), .clk(clock), .Q(pc_value), .clr(pc_reset));
endmodule

module InstructionRegister (
  input  clock,
  input  ir_load,
  input  [7:0] data_in,
  output [7:0] ir_value
);

  Register IR (.D(data_in), .en(ir_load), .clk(clock), .Q(ir_value));  // open: clr
endmodule

module OperandRegister (
  input  clock,
  input  operand_load,
  input  [7:0] data_in,
  output [7:0] operand_value
);

  Register OpReg (.D(data_in), .en(operand_load), .clk(clock), .Q(operand_value));  // open: clr
endmodule

module Memory (
  input  [7:0] address,
  input  write_enable,
  input  clock,
  input  [7:0] write_data,
  input  output_enable,
  output [7:0] read_data
);

  RAM #(.asyncread("true"), .\type ("nonvolatile")) RAM1 (
    .addr(address), .we(write_enable), .oe(output_enable), .clk(clock), .din(write_data), .dout(read_data));
endmodule

module Control (
  input  [7:0] instruction,
  input  clock,
  input  reset,
  output pc_increment,
  output ir_load,
  output operand_load,
  output pc_load,
  output conditional_jump,
  output memory_write,
  output [2:0] State,
  output register_write
);

  wire comparator_1_eq, comparator_2_eq, comparator_3_eq, comparator_4_eq, comparator_5_eq, comparator_6_eq,
       comparator_7_eq, comparator_8_eq, comparator_9_eq, comparator_10_eq, comparator_11_eq,
       comparator_12_eq, comparator_15_eq, comparator_16_eq, comparator_17_eq, comparator_18_eq, or_1_out,
       or_2_out;
  wire [2:0] multiplexer_1_out, multiplexer_2_out, multiplexer_3_out;

  Comparator #(.width(4)) comparator_1 (.a(4'b1100), .b(instruction[7:4]), .eq(comparator_1_eq));  // open: gt, lt
  Comparator #(.mode("unsigned"), .width(4)) comparator_2 (
    .a(instruction[7:4]), .b(4'b0101), .eq(comparator_2_eq));  // open: gt, lt
  Comparator #(.mode("unsigned"), .width(4)) comparator_3 (
    .a(instruction[7:4]), .b(4'b1010), .eq(comparator_3_eq));  // open: gt, lt
  Comparator #(.mode("unsigned"), .width(4)) comparator_4 (
    .a(instruction[7:4]), .b(4'b1011), .eq(comparator_4_eq));  // open: gt, lt
  Comparator #(.mode("unsigned"), .width(4)) comparator_5 (
    .a(instruction[7:4]), .b(4'b1101), .eq(comparator_5_eq));  // open: gt, lt
  Comparator #(.mode("unsigned"), .width(4)) comparator_6 (
    .a(instruction[7:4]), .b(4'b1110), .eq(comparator_6_eq));  // open: gt, lt
  Multiplexer #(.width(3)) multiplexer_1 (.in0(3'b000), .in1(3'b100), .out(multiplexer_1_out), .sel(comparator_1_eq));
  or or_1 (or_1_out, comparator_2_eq, comparator_3_eq, comparator_4_eq, comparator_5_eq, comparator_6_eq);
  Multiplexer #(.width(3)) multiplexer_2 (.in0(3'b011), .in1(3'b010), .out(multiplexer_2_out), .sel(or_1_out));
  Multiplexer #(.select(3), .width(3)) multiplexer_3 (
    .in0(3'b001), .in1(multiplexer_2_out), .in2(3'b011), .in3(multiplexer_1_out), .in4(3'b100),
    .in5(multiplexer_1_out), .in6(multiplexer_1_out), .in7(multiplexer_1_out), .out(multiplexer_3_out),
    .sel(State));
  Register #(.width(3)) StateReg (.D(multiplexer_3_out), .en(1'b1), .clk(clock), .Q(State), .clr(reset));
  Comparator #(.mode("unsigned"), .width(4)) comparator_7 (
    .a(4'b0101), .b(instruction[7:4]), .eq(comparator_7_eq));  // open: gt, lt
  Comparator #(.mode("unsigned"), .width(4)) comparator_8 (
    .a(4'b0110), .b(instruction[7:4]), .eq(comparator_8_eq));  // open: gt, lt
  Comparator #(.mode("unsigned"), .width(4)) comparator_9 (
    .a(4'b0111), .b(instruction[7:4]), .eq(comparator_9_eq));  // open: gt, lt
  Comparator #(.mode("unsigned"), .width(4)) comparator_10 (
    .a(4'b1000), .b(instruction[7:4]), .eq(comparator_10_eq));  // open: gt, lt
  Comparator #(.mode("unsigned"), .width(4)) comparator_11 (
    .a(4'b1001), .b(instruction[7:4]), .eq(comparator_11_eq));  // open: gt, lt
  Comparator #(.mode("unsigned"), .width(4)) comparator_12 (
    .a(4'b1101), .b(instruction[7:4]), .eq(comparator_12_eq));  // open: gt, lt
  Comparator #(.mode("unsigned"), .width(3)) comparator_13 (.a(3'b000), .b(State), .eq(ir_load));  // open: gt, lt
  Comparator #(.mode("unsigned"), .width(3)) comparator_14 (.a(3'b010), .b(State), .eq(operand_load));  // open: gt, lt
  Comparator #(.mode("unsigned"), .width(3)) comparator_15 (
    .a(3'b011), .b(State), .eq(comparator_15_eq));  // open: gt, lt
  Comparator #(.mode("unsigned"), .width(4)) comparator_16 (
    .a(4'b1010), .b(instruction[7:4]), .eq(comparator_16_eq));  // open: gt, lt
  Comparator #(.mode("unsigned"), .width(4)) comparator_17 (
    .a(4'b1011), .b(instruction[7:4]), .eq(comparator_17_eq));  // open: gt, lt
  Comparator #(.mode("unsigned"), .width(4)) comparator_18 (
    .a(4'b1110), .b(instruction[7:4]), .eq(comparator_18_eq));  // open: gt, lt
  or or_2 (or_2_out, comparator_7_eq, comparator_8_eq, comparator_9_eq, comparator_10_eq, comparator_11_eq, comparator_12_eq);
  or or_3 (pc_increment, ir_load, operand_load);
  and and_1 (pc_load, comparator_15_eq, comparator_16_eq);
  and and_2 (conditional_jump, comparator_15_eq, comparator_17_eq);
  and and_3 (memory_write, comparator_15_eq, comparator_18_eq);
  and and_4 (register_write, comparator_15_eq, or_2_out);
endmodule

module CPU (
  input  clock,
  input  reset,
  output [7:0] pc_value_op,
  output [7:0] memory_read_data_op,
  output [7:0] ir_value_op,
  output [7:0] operand_reg_val_op,
  output [1:0] t2,
  output [1:0] t1,
  output t3,
  output [2:0] Control_state_op
);

  wire alu_1_zero, and_1_out, and_2_out, and_3_out, comparator_1_eq, comparator_2_eq, comparator_3_eq,
       comparator_4_eq, comparator_5_eq, comparator_6_eq, comparator_7_eq, comparator_8_eq, comparator_9_eq,
       comparator_10_eq, Control1_conditional_jump, Control1_ir_load, Control1_memory_write,
       Control1_operand_load, Control1_pc_increment, Control1_pc_load, Control1_register_write, or_3_out,
       or_4_out, or_5_out;
  wire [7:0] alu_1_result, multiplexer_1_out, multiplexer_2_out, Registers1_read_data_a,
       Registers1_read_data_b;

  PC pc_1 (
    .clock(clock), .pc_increment(Control1_pc_increment), .pc_load(or_5_out),
    .pc_load_value(operand_reg_val_op), .pc_reset(reset), .pc_value(pc_value_op));
  Memory Memory1 (
    .address(multiplexer_1_out), .write_enable(Control1_memory_write), .clock(clock),
    .write_data(Registers1_read_data_a), .output_enable(1'b1), .read_data(memory_read_data_op));
  InstructionRegister IR1 (
    .clock(clock), .ir_load(Control1_ir_load), .data_in(memory_read_data_op), .ir_value(ir_value_op));
  OperandRegister OpReg (
    .clock(clock), .operand_load(Control1_operand_load), .data_in(memory_read_data_op),
    .operand_value(operand_reg_val_op));
  Registers Registers1 (
    .clock(clock), .write_enable(Control1_register_write), .write_addr(ir_value_op[3:2]),
    .write_data(multiplexer_2_out), .read_addr_a(ir_value_op[3:2]), .read_addr_b(ir_value_op[1:0]),
    .read_data_a(Registers1_read_data_a), .read_data_b(Registers1_read_data_b));
  Control Control1 (
    .instruction(ir_value_op), .clock(clock), .reset(reset), .pc_increment(Control1_pc_increment),
    .ir_load(Control1_ir_load), .operand_load(Control1_operand_load), .pc_load(Control1_pc_load),
    .conditional_jump(Control1_conditional_jump), .memory_write(Control1_memory_write),
    .State(Control_state_op), .register_write(Control1_register_write));
  Multiplexer #(.width(8)) multiplexer_1 (
    .in0(pc_value_op), .in1(operand_reg_val_op), .out(multiplexer_1_out), .sel(and_2_out));
  Comparator #(.mode("unsigned"), .width(4)) comparator_1 (
    .a(ir_value_op[7:4]), .b(4'b0111), .eq(comparator_1_eq));  // open: gt, lt
  Comparator #(.mode("unsigned"), .width(4)) comparator_2 (
    .a(ir_value_op[7:4]), .b(4'b1000), .eq(comparator_2_eq));  // open: gt, lt
  Comparator #(.mode("unsigned"), .width(4)) comparator_3 (
    .a(ir_value_op[7:4]), .b(4'b1001), .eq(comparator_3_eq));  // open: gt, lt
  or or_1 (t1[0], comparator_1_eq, comparator_3_eq);
  or or_2 (t1[1], comparator_2_eq, comparator_3_eq);
  Multiplexer #(.select(2), .width(8)) multiplexer_2 (
    .in0(alu_1_result), .in1(operand_reg_val_op), .in2(memory_read_data_op), .in3({8{1'b0}}),
    .out(multiplexer_2_out), .sel(t2));
  Comparator #(.width(4)) comparator_4 (.a(ir_value_op[7:4]), .b(4'b1101), .eq(comparator_4_eq));  // open: gt, lt
  Comparator #(.width(4)) comparator_5 (.a(ir_value_op[7:4]), .b(4'b1110), .eq(comparator_5_eq));  // open: gt, lt
  ALU alu_1 (
    .A(Registers1_read_data_a), .B(Registers1_read_data_b), .Operation(t1), .Result(alu_1_result),
    .Zero(alu_1_zero));
  Register #(.width(1)) register_1 (.D(alu_1_zero), .en(and_3_out), .clk(clock), .Q(t3), .clr(reset));
  or or_3 (or_3_out, comparator_4_eq, comparator_5_eq);
  Comparator #(.mode("unsigned"), .width(4)) comparator_6 (
    .a(ir_value_op[7:4]), .b(4'b0110), .eq(comparator_6_eq));  // open: gt, lt
  Comparator #(.mode("unsigned"), .width(4)) comparator_7 (
    .a(ir_value_op[7:4]), .b(4'b0111), .eq(comparator_7_eq));  // open: gt, lt
  Comparator #(.mode("unsigned"), .width(4)) comparator_8 (
    .a(ir_value_op[7:4]), .b(4'b1000), .eq(comparator_8_eq));  // open: gt, lt
  Comparator #(.mode("unsigned"), .width(4)) comparator_9 (
    .a(ir_value_op[7:4]), .b(4'b1001), .eq(comparator_9_eq));  // open: gt, lt
  Comparator #(.mode("unsigned"), .width(3)) comparator_10 (
    .a(3'b011), .b(Control_state_op), .eq(comparator_10_eq));  // open: gt, lt
  and and_1 (and_1_out, t3, Control1_conditional_jump);
  or or_4 (or_4_out, comparator_6_eq, comparator_7_eq, comparator_8_eq, comparator_9_eq);
  and and_2 (and_2_out, comparator_10_eq, or_3_out);
  Comparator #(.width(4)) comparator_11 (.a(ir_value_op[7:4]), .b(4'b0101), .eq(t2[0]));  // open: gt, lt
  Comparator #(.width(4)) comparator_12 (.a(4'b1101), .b(ir_value_op[7:4]), .eq(t2[1]));  // open: gt, lt
  or or_5 (or_5_out, Control1_pc_load, and_1_out);
  and and_3 (and_3_out, Control1_register_write, or_4_out);
endmodule
